# Fritzing sketch data-emitor-esp32-can-bosch (saved by Fritzing 1.0.6)
breadboards: 1

parts:
  Part1 = ADS1115  # not connected
  M1 = SN65HVD230 CAN Bus transciever module [package=THT]
  A1 = ESP32-C6-DevKitC-1
  R1 = Resistor [tolerance=±5% resistance=4700 package="0805 [SMD]"]
  MPX1 = MPX2010 pressure sensor [part_number=MPX]
  S1 = SWITCH-MOMENTARY-2 [package=tactile-pth]
  U1 = Mini-360 DC-DC Buck converter [package=THT]
  Power_plug1 = Power plug

nets:
  N1: M1.pin_2, MPX1.GND, S1.2
  N2: M1.pin_3, A1.Pin_11
  N3: M1.pin_4, A1.Pin_10
  N4: A1.Pin_8, S1.1
  N5: A1.Pin_15, A1.Pin_18, A1.Pin_32, U1.OUT-
  N6: R1.Pin_0, MPX1.V_out_-
  N7: R1.Pin_1, MPX1.V_out_+
  N8: U1.IN-, Power_plug1.GND
  N9: U1.IN+, Power_plug1.VCC

notes:
  Bosch Pressure and Temp sensor:
  5V
  Blue = Resistor for temp
  White = current for pressure

custom parts:
  ADS1115: ADC ADS1115
  SN65HVD230 CAN Bus transciever module: Bus Transceiver SN65HVD230 CAN Communication Module, for Arduino.
  ESP32-C6-DevKitC-1: ESP32-C6-DevKitC-1 is an entry-level development board based on ESP32-C6-WROOM-1(U), a general-purpose module with a 8 MB SPI flash. This board integrates complete Wi-Fi, Bluetooth LE, Zigbee, and Thread functions.
  Mini-360 DC-DC Buck converter: Mini-360 DC-DC Buck converter. Tiny buck step down voltage converter, input voltage 4.75 to 23V output 1 to 17V adjustable. Available from ebay and the like.
